// Logisim project PipelinedRISC.circ as structural Verilog: 14 circuits, main circuit main
module main (
);

  wire alusrc, alusrc_2, alusrc_3, alusrc_4, bbflag, bbflag_4, clock_1_out, delay_79_buffer_1_out,
       delay_79_buffer_2_out, delay_79_buffer_3_out, delay_79_buffer_4_out, hazard_unit_1_clear,
       hazard_unit_1_stall, not_1_out, r1, r1_2, r1_3, r1_4, r7, r7_2, r7_3, r7_4, sri, sri_2, sri_3, sri_4,
       store, store_2, store_3, stri, stri_2, stri_3, stri_4, write, write_2, write_3, write_4;
  wire [1:0] func2, func2_2, func2_3;
  wire [2:0] rd3, rd3_2, rs3, rs3_2, rt3, rt3_2, w_register, w_register_3, w_register_4;
  wire [4:0] imm5, imm5_2, imm5_3, imm5_4, opcode, opcode_2, opcode_3;
  wire [10:0] imm11, imm11_2, imm11_3;
  wire [11:0] fdj_1_pc_output, pc_1, pc_1_2, pc_1_3, pc_1_4;
  wire [15:0] alu_out, alu_out_4, instr_input, instr_input_1, mem_out, mem_out_4, r_input, rs, rs_3, rt, rt_3;

  Clock clock_1 (.out(clock_1_out));
  _1st_stage u_1st_stage_1 (
    .instr_input(instr_input), .clock(clock_1_out), .stall(hazard_unit_1_stall), .clear(hazard_unit_1_clear),
    .instr_input_2(instr_input_1));
  RAM #(.addrWidth(12), .dataWidth(16), .bus("separate")) ram_1 (
    .addr(fdj_1_pc_output), .data(instr_input));  // open: din, str, sel, clk, ld, clr
  FDJ fdj_1 (
    .PC_1_branch(pc_1), .PC_output(fdj_1_pc_output), .rt3(rt3), .rs3(rs3), .rd3(rd3), .func2(func2),
    .immediate5(imm5), .immediate11(imm11), .opcode(opcode), .instruction_input(instr_input_1),
    .clock(clock_1_out), .address_from_alu(alu_out), .imm5(imm5_3), .beq_bne_flag(bbflag),
    .address_from_rs_3(rs_3));
  Delay_79_Buffer delay_79_buffer_1 (.in(clock_1_out), .out(delay_79_buffer_1_out));
  _2nd_stage u_2nd_stage_1 (
    .clock(delay_79_buffer_1_out), .stall(hazard_unit_1_stall), .rd3(rd3), .rt3(rt3), .rs3(rs3),
    .pc_1_branch(pc_1), .func2(func2), .immediate5(imm5), .immediate11(imm11), .opcode(opcode),
    .r7_write(r7), .write(write), .single_reg_instr(sri), .single_third_reg_instr(stri), .r1_write(r1),
    .alu_source(alusrc), .store_memory(store), .clear(hazard_unit_1_clear), .rd3_2(rd3_2), .rt3_2(rt3_2),
    .rs3_2(rs3_2), .pc_1_branch_2(pc_1_2), .func2_2(func2_2), .immediate5_2(imm5_2), .immediate11_2(imm11_2),
    .opcode_2(opcode_2), .r7_write_2(r7_2), .write_2(write_2), .single_reg_instr_2(sri_2),
    .single_third_reg_instr_2(stri_2), .r1_write_2(r1_2), .alu_source_2(alusrc_2), .store_memory_2(store_2));
  Control_Unit control_unit_1 (
    .opcode(opcode), .clock(clock_1_out), .write(write), .alu_source(alusrc), .single_reg_instr(sri),
    .store_memory(store), .single_third_reg_instr(stri), .r1_write(r1), .r7_write(r7));
  REG reg_1 (
    .r1_write(r1_4), .\input (r_input), .write_register_rd(rd3_2), .rt3(rt3_2), .rs3(rs3_2), .write(write_4),
    .output_0(rt), .output_1(rs), .single_third_reg_instr(stri_2), .single_reg_instr(sri_2), .r7_write(r7_4),
    .pc_1_input(pc_1_4), .write_register_2(w_register), .write_register(w_register_4));
  Delay_79_Buffer delay_79_buffer_2 (.in(clock_1_out), .out(delay_79_buffer_2_out));
  hazard_unit hazard_unit_1 (
    .opcode_3(opcode_3), .beq_bne_flag(bbflag_4), .stall(hazard_unit_1_stall), .clear(hazard_unit_1_clear));
  _3rd_stage u_3rd_stage_1 (
    .clock(delay_79_buffer_2_out), .stall(hazard_unit_1_stall), .pc_1_branch(pc_1_2), .output_0(rt),
    .output_1(rs), .func2(func2_2), .imm5(imm5_2), .imm11(imm11_2), .opcode(opcode_2),
    .store_memory(store_2), .alu_source(alusrc_2), .write_register(w_register), .r7_write(r7_2),
    .write(write_2), .single_reg_instr(sri_2), .single_third_reg_instr(stri_2), .r1_write(r1_2),
    .clear(hazard_unit_1_clear), .pc_1_branch_2(pc_1_3), .output_0_2(rt_3), .output_1_2(rs_3),
    .func2_2(func2_3), .imm5_2(imm5_3), .imm11_2(imm11_3), .opcode_2(opcode_3), .store_memory_2(store_3),
    .alu_source_2(alusrc_3), .write_register_2(w_register_3), .r7_write_2(r7_3), .write_2(write_3),
    .single_reg_instr_2(sri_3), .single_third_reg_instr_2(stri_3), .r1_write_2(r1_3));
  Register #(.width(1), .trigger("high")) register_1 (
    .D(hazard_unit_1_clear), .en(hazard_unit_1_clear), .clk(1'b1));  // open: Q, clr
  ALU alu_1 (
    .func2(func2_3), .Immadiate5(imm5_3), .Immadiate11(imm11_3), .Rs(rs_3), .Rt(rt_3), .Opcode(opcode_3),
    .Output(alu_out));
  alu_mem_MUX alu_mem_mux_1 (
    .register_input(r_input), .alu_source(alusrc_4), .memory_output(mem_out_4), .alu_output(alu_out_4));
  Delay_79_Buffer delay_79_buffer_3 (.in(clock_1_out), .out(delay_79_buffer_3_out));
  _4th_stage u_4th_stage_1 (
    .clock(delay_79_buffer_3_out), .stall(hazard_unit_1_stall), .pc_1_branch(pc_1_3), .alu_source(alusrc_3),
    .alu_output(alu_out), .memory_output(mem_out), .write_register(w_register_3), .r7_write(r7_3),
    .write(write_3), .single_reg_instr(sri_3), .single_third_reg_instr(stri_3), .r1_write(r1_3),
    .imm5(imm5_3), .bb(bbflag), .pc_1_branch_2(pc_1_4), .alu_source_2(alusrc_4), .alu_output_2(alu_out_4),
    .memory_output_2(mem_out_4), .write_register_2(w_register_4), .r7_write_2(r7_4), .write_2(write_4),
    .single_reg_instr_2(sri_4), .single_third_reg_instr_2(stri_4), .r1_write_2(r1_4), .imm5_2(imm5_4),
    .bb_2(bbflag_4));  // open: clear
  Delay_79_Buffer delay_79_buffer_4 (.in(store_3), .out(delay_79_buffer_4_out));
  not not_1 (not_1_out, store_3);
  RAM #(.addrWidth(16), .dataWidth(16), .bus("separate")) ram_2 (
    .addr(alu_out), .din(rt_3), .data(mem_out), .clk(delay_79_buffer_4_out), .ld(not_1_out));  // open: str, sel, clr

  // Notes on the sheet:
  //   stall = 0
  //   clear error catch
endmodule

module FDJ (
  input  [4:0] imm5,
  input  [15:0] instruction_input,
  input  clock,
  input  [15:0] address_from_rs_3,
  input  [15:0] address_from_alu,
  output [2:0] rt3,
  output [2:0] rs3,
  output [2:0] rd3,
  output [1:0] func2,
  output [11:0] PC_1_branch,
  output [4:0] immediate5,
  output [11:0] PC_output,
  output [10:0] immediate11,
  output [4:0] opcode,
  output beq_bne_flag
);

  wire BEQ_BNE_out, delay_79_buffer_1_out, JAL_out, JR_out, jump_out, not_1_out, not_2_out, not_3_out,
       not_4_out, not_5_out, not_6_out, or_1_out, register_1_q, register_2_q, register_3_q, register_4_q;
  wire [11:0] adder_1_out, adder_2_out, adder_3_out, bit_extender_1_out, bit_extender_2_out,
       multiplexer_1_out, multiplexer_2_out, multiplexer_3_out;

  Multiplexer #(.width(12), .enable("false")) multiplexer_1 (
    .in0(multiplexer_2_out), .in1(adder_3_out), .out(multiplexer_1_out), .sel(beq_bne_flag));
  Register #(.width(12)) PC (.D(multiplexer_1_out), .Q(PC_output), .clk(clock));  // open: en, clr
  assign bit_extender_1_out = {{7{imm5[4]}}, imm5};  // Bit_Extender bit_extender_1
  Multiplexer #(.width(12), .enable("false")) multiplexer_2 (
    .in0(multiplexer_3_out), .in1(adder_1_out), .out(multiplexer_2_out), .sel(or_1_out));
  Adder #(.width(12)) adder_1 (.a(bit_extender_2_out), .b(PC_output), .out(adder_1_out));  // open: cin, cout
  Adder #(.width(12)) adder_2 (.a(PC_output), .b(12'h1), .out(adder_2_out));  // open: cin, cout
  Adder #(.width(12)) adder_3 (.a(PC_output), .b(bit_extender_1_out), .out(adder_3_out));  // open: cin, cout
  Multiplexer #(.width(12), .enable("false")) multiplexer_3 (
    .in0(adder_2_out), .in1(address_from_rs_3[11:0]), .out(multiplexer_3_out), .sel(register_2_q));
  Register #(.width(12)) PC_1 (.D(adder_2_out), .Q(PC_1_branch), .clk(clock));  // open: en, clr
  not not_1 (not_1_out, instruction_input[15]);
  not not_2 (not_2_out, instruction_input[14]);
  Register #(.width(1)) register_1 (.D(JR_out), .Q(register_1_q), .clk(delay_79_buffer_1_out));  // open: en, clr
  Delay_79_Buffer delay_79_buffer_1 (.in(clock), .out(delay_79_buffer_1_out));
  assign bit_extender_2_out = {{1{instruction_input[10]}}, instruction_input[10:0]};  // Bit_Extender bit_extender_2
  not not_3 (not_3_out, instruction_input[11]);
  not not_4 (not_4_out, instruction_input[13]);
  and JR (JR_out, not_1_out, not_2_out, not_4_out, instruction_input[12], not_3_out);
  and jump (jump_out, instruction_input[15], instruction_input[14], instruction_input[13], instruction_input[12], not_5_out);
  Register #(.width(1)) register_2 (.D(register_1_q), .Q(register_2_q), .clk(delay_79_buffer_1_out));  // open: en, clr
  not not_5 (not_5_out, instruction_input[11]);
  and JAL (JAL_out, instruction_input[15], instruction_input[14], instruction_input[13], instruction_input[12], instruction_input[11]);
  or or_1 (or_1_out, jump_out, JAL_out);
  not not_6 (not_6_out, instruction_input[15]);
  and BEQ_BNE (BEQ_BNE_out, not_6_out, instruction_input[14], instruction_input[13], instruction_input[12]);
  Register #(.width(1)) register_3 (.D(BEQ_BNE_out), .Q(register_3_q), .clk(delay_79_buffer_1_out));  // open: en, clr
  Register #(.width(1)) register_4 (.D(register_3_q), .Q(register_4_q), .clk(delay_79_buffer_1_out));  // open: en, clr
  and and_1 (beq_bne_flag, register_4_q, address_from_alu[0]);

  assign func2 = instruction_input[10:9];
  assign immediate5 = instruction_input[10:6];
  assign immediate11 = instruction_input[10:0];
  assign opcode = instruction_input[15:11];
  assign rd3 = instruction_input[8:6];
  assign rs3 = instruction_input[5:3];
  assign rt3 = instruction_input[2:0];

  // Notes on the sheet:
  //   immediate adress
endmodule

module REG (
  input  r1_write,
  input  [15:0] \input ,
  input  [11:0] pc_1_input,
  input  [2:0] write_register_rd,
  input  [2:0] write_register,
  input  [2:0] rt3,
  input  single_reg_instr,
  input  [2:0] rs3,
  input  single_third_reg_instr,
  input  write,
  input  r7_write,
  output [15:0] output_0,
  output [2:0] write_register_2,
  output [15:0] output_1
);

  wire and_1_out, and_2_out, and_3_out, and_4_out, and_5_out, and_6_out, and_7_out, and_8_out, not_1_out,
       not_2_out, not_3_out, not_4_out, not_5_out, not_6_out, not_7_out, not_8_out, not_9_out, not_10_out,
       not_11_out, not_12_out, not_13_out, not_14_out, or_1_out, or_2_out;
  wire [2:0] multiplexer_1_out;
  wire [15:0] bit_extender_1_out, multiplexer_3_out, register_1_q, register_2_q, register_3_q, register_4_q,
       register_5_q, register_6_q, register_7_q, register_8_q;

  Multiplexer #(.width(3), .enable("false")) multiplexer_1 (
    .in0(write_register_rd), .in1(rt3), .out(multiplexer_1_out), .sel(single_reg_instr));
  Multiplexer #(.width(3), .enable("false")) multiplexer_2 (
    .in0(multiplexer_1_out), .in1(rs3), .out(write_register_2), .sel(single_third_reg_instr));
  not not_1 (not_1_out, r7_write);
  not not_2 (not_2_out, r1_write);
  not not_3 (not_3_out, write_register[0]);
  not not_4 (not_4_out, write_register[1]);
  not not_5 (not_5_out, write_register[2]);
  not not_6 (not_6_out, write_register[1]);
  not not_7 (not_7_out, write_register[2]);
  not not_8 (not_8_out, write_register[0]);
  not not_9 (not_9_out, write_register[2]);
  not not_10 (not_10_out, write_register[2]);
  not not_11 (not_11_out, write_register[0]);
  not not_12 (not_12_out, write_register[1]);
  not not_13 (not_13_out, write_register[1]);
  not not_14 (not_14_out, write_register[0]);
  and and_1 (and_1_out, not_1_out, not_3_out, not_4_out, not_5_out, not_2_out, write);
  and and_2 (and_2_out, not_1_out, write_register[0], not_6_out, not_7_out, write);
  and and_3 (and_3_out, not_1_out, not_8_out, write_register[1], not_9_out, not_2_out, write);
  and and_4 (and_4_out, not_1_out, write_register[0], write_register[1], not_10_out, not_2_out, write);
  and and_5 (and_5_out, not_1_out, not_11_out, not_12_out, write_register[2], not_2_out, write);
  and and_6 (and_6_out, not_1_out, write_register[0], not_13_out, write_register[2], not_2_out, write);
  and and_7 (and_7_out, not_1_out, not_14_out, write_register[1], write_register[2], not_2_out, write);
  and and_8 (and_8_out, write_register[0], write_register[1], write_register[2], not_2_out, write);
  or or_1 (or_1_out, r1_write, and_2_out);
  or or_2 (or_2_out, and_8_out, r7_write);
  Register #(.width(16), .trigger("high")) register_1 (
    .D({16{1'b0}}), .Q(register_1_q), .clk(and_1_out));  // open: en, clr
  Register #(.width(16), .trigger("high")) register_2 (.D(\input ), .Q(register_2_q), .clk(or_1_out));  // open: en, clr
  Register #(.width(16), .trigger("high")) register_3 (
    .D(\input ), .Q(register_3_q), .clk(and_3_out));  // open: en, clr
  Register #(.width(16), .trigger("high")) register_4 (
    .D(\input ), .Q(register_4_q), .clk(and_4_out));  // open: en, clr
  Register #(.width(16), .trigger("high")) register_5 (
    .D(\input ), .Q(register_5_q), .clk(and_5_out));  // open: en, clr
  Register #(.width(16), .trigger("high")) register_6 (
    .D(\input ), .Q(register_6_q), .clk(and_6_out));  // open: en, clr
  Register #(.width(16), .trigger("high")) register_7 (
    .D(\input ), .Q(register_7_q), .clk(and_7_out));  // open: en, clr
  Multiplexer #(.width(16), .enable("false")) multiplexer_3 (
    .in0(\input ), .in1(bit_extender_1_out), .out(multiplexer_3_out), .sel(r7_write));
  Register #(.width(16), .trigger("high")) register_8 (
    .D(multiplexer_3_out), .Q(register_8_q), .clk(or_2_out));  // open: en, clr
  assign bit_extender_1_out = {{4{1'b0}}, pc_1_input};  // Bit_Extender bit_extender_1
  Multiplexer #(.select(3), .width(16), .enable("false")) multiplexer_4 (
    .in0(register_1_q), .in1(register_2_q), .in2(register_3_q), .in3(register_4_q), .in4(register_5_q),
    .in5(register_6_q), .in6(register_7_q), .in7(register_8_q), .out(output_0), .sel(rt3));
  Multiplexer #(.select(3), .width(16), .enable("false")) multiplexer_5 (
    .in0(register_1_q), .in1(register_2_q), .in2(register_3_q), .in3(register_4_q), .in4(register_5_q),
    .in5(register_6_q), .in6(register_7_q), .in7(register_8_q), .out(output_1), .sel(rs3));
endmodule

// CONTROL
module Control_Unit (
  input  [4:0] opcode,
  input  clock,
  output write,
  output r1_write,
  output alu_source,
  output single_reg_instr,
  output single_third_reg_instr,
  output r7_write,
  output store_memory
);

  wire and_2_out, and_5_out, and_6_out, and_7_out, and_8_out, and_9_out, and_10_out, not_1_out, not_2_out,
       not_3_out, not_4_out, not_5_out, not_6_out, not_7_out, not_8_out, not_9_out, not_10_out, not_11_out,
       not_12_out, not_13_out, not_14_out, not_15_out, not_16_out, not_17_out, not_18_out, not_19_out,
       not_20_out, not_21_out, not_22_out, not_23_out, or_1_out, or_2_out, or_3_out;

  and and_1 (r1_write, opcode[4], not_1_out, not_2_out, not_7_out, not_6_out);
  not not_1 (not_1_out, opcode[3]);
  not not_2 (not_2_out, opcode[2]);
  and and_2 (and_2_out, opcode[1], opcode[3], opcode[2], not_3_out);
  not not_3 (not_3_out, opcode[4]);
  not not_4 (not_4_out, opcode[1]);
  not not_5 (not_5_out, opcode[4]);
  not not_6 (not_6_out, opcode[0]);
  not not_7 (not_7_out, opcode[1]);
  not not_8 (not_8_out, opcode[3]);
  not not_9 (not_9_out, opcode[4]);
  and and_3 (r7_write, opcode[0], opcode[1], opcode[2], opcode[3], opcode[4]);
  and and_4 (store_memory, opcode[0], not_4_out, opcode[2], opcode[3], not_5_out);
  and and_5 (and_5_out, opcode[2], not_8_out, not_9_out);
  not not_10 (not_10_out, opcode[0]);
  not not_11 (not_11_out, opcode[1]);
  not not_12 (not_12_out, opcode[2]);
  not not_13 (not_13_out, opcode[3]);
  not not_14 (not_14_out, opcode[4]);
  not not_15 (not_15_out, opcode[1]);
  not not_16 (not_16_out, opcode[2]);
  not not_17 (not_17_out, opcode[3]);
  not not_18 (not_18_out, opcode[4]);
  not not_19 (not_19_out, opcode[2]);
  and and_6 (and_6_out, not_19_out, opcode[3], not_20_out);
  not not_20 (not_20_out, opcode[4]);
  not not_21 (not_21_out, opcode[0]);
  not not_22 (not_22_out, opcode[1]);
  and and_7 (and_7_out, not_21_out, not_22_out, opcode[2], opcode[3], not_23_out);
  not not_23 (not_23_out, opcode[4]);
  and and_8 (and_8_out, not_10_out, not_11_out, not_12_out, not_13_out, not_14_out);
  and and_9 (and_9_out, opcode[0], not_15_out, not_16_out, not_17_out, not_18_out);
  or or_1 (or_1_out, and_5_out, and_6_out);
  or or_2 (or_2_out, r1_write, and_8_out, and_7_out, or_1_out, and_9_out, r7_write);
  or or_3 (or_3_out, r1_write, and_8_out, or_1_out, and_9_out, store_memory);
  and and_10 (and_10_out, or_2_out, clock);
  buf or_4 (single_third_reg_instr, 1'b0);  // OR_Gate
  or or_5 (single_reg_instr, or_1_out, and_7_out);
  and and_11 (alu_source, or_3_out, clock);
  or or_6 (write, and_7_out, and_10_out);
endmodule

module ALU (
  input  [15:0] Rs,
  input  [15:0] Rt,
  input  [1:0] func2,
  input  [4:0] Immadiate5,
  input  [4:0] Opcode,
  input  [10:0] Immadiate11,
  output [15:0] Output
);

  wire comparator_1_lt, comparator_2_eq, comparator_2_lt, not_1_out;
  wire [15:0] adder_1_out, adder_2_out, and_1_out, and_2_out, bit_extender_1_out, bit_extender_2_out,
       bit_extender_3_out, bit_extender_4_out, bit_extender_5_out, bit_extender_6_out, bit_extender_7_out,
       bit_extender_8_out, multiplexer_1_out, multiplexer_2_out, nor_1_out, or_1_out, or_2_out,
       shifter_1_out, shifter_2_out, shifter_3_out, shifter_4_out, shifter_5_out, subtractor_1_out,
       xor_1_out, xor_2_out;

  assign bit_extender_1_out = {{11{1'b0}}, Immadiate5};  // Bit_Extender bit_extender_1
  Bit_Extender #(.in_width(16), .\type ("sign")) bit_extender_2 (.in(Rs), .out(bit_extender_2_out));
  Bit_Extender #(.in_width(16), .\type ("one")) bit_extender_3 (.in(Rt), .out(bit_extender_3_out));
  assign bit_extender_4_out = {{5{1'b0}}, Immadiate11};  // Bit_Extender bit_extender_4
  assign and_1_out = Rs & Rt;  // AND_Gate and_1, 16 bits wide
  assign or_1_out = Rs | Rt;  // OR_Gate or_1, 16 bits wide
  assign xor_1_out = Rs ^ Rt;  // XOR_Gate xor_1, 16 bits wide
  assign nor_1_out = ~(Rs | Rt);  // NOR_Gate nor_1, 16 bits wide
  Adder #(.width(16)) adder_1 (.a(Rs), .b(Rt), .out(adder_1_out));  // open: cin, cout
  Subtractor #(.width(16)) subtractor_1 (.a(Rs), .b(Rt), .out(subtractor_1_out));  // open: bin, bout
  Comparator #(.width(16)) comparator_1 (
    .a(bit_extender_2_out), .b(bit_extender_3_out), .lt(comparator_1_lt));  // open: gt, eq
  Comparator #(.width(16), .mode("unsigned")) comparator_2 (
    .a(Rs), .b(Rt), .eq(comparator_2_eq), .lt(comparator_2_lt));  // open: gt
  assign and_2_out = Rs & bit_extender_1_out;  // AND_Gate and_2, 16 bits wide
  assign or_2_out = Rs | bit_extender_1_out;  // OR_Gate or_2, 16 bits wide
  assign xor_2_out = Rs ^ bit_extender_1_out;  // XOR_Gate xor_2, 16 bits wide
  Adder #(.width(16)) adder_2 (.a(Rs), .b(bit_extender_1_out), .out(adder_2_out));  // open: cin, cout
  Shifter #(.width(16)) shifter_1 (.in(Rs), .\dist (Immadiate5[3:0]), .out(shifter_1_out));
  Shifter #(.width(16), .shift("lr")) shifter_2 (.in(Rs), .\dist (Immadiate5[3:0]), .out(shifter_2_out));
  Shifter #(.width(16), .shift("ar")) shifter_3 (.in(Rs), .\dist (Immadiate5[3:0]), .out(shifter_3_out));
  Shifter #(.width(16), .shift("rr")) shifter_4 (.in(Rs), .\dist (Immadiate5[3:0]), .out(shifter_4_out));
  Shifter #(.width(16)) shifter_5 (.in(bit_extender_4_out), .\dist (4'b0101), .out(shifter_5_out));
  assign bit_extender_5_out = {{15{1'b0}}, comparator_1_lt};  // Bit_Extender bit_extender_5
  assign bit_extender_6_out = {{15{1'b0}}, comparator_2_lt};  // Bit_Extender bit_extender_6
  Multiplexer #(.select(2), .width(16)) multiplexer_1 (
    .in0(adder_1_out), .in1(subtractor_1_out), .in2(bit_extender_5_out), .in3(bit_extender_6_out),
    .out(multiplexer_1_out), .sel(func2));  // open: en
  assign bit_extender_7_out = {{15{1'b0}}, comparator_2_eq};  // Bit_Extender bit_extender_7
  not not_1 (not_1_out, comparator_2_eq);
  assign bit_extender_8_out = {{15{1'b0}}, not_1_out};  // Bit_Extender bit_extender_8
  Multiplexer #(.select(2), .width(16)) multiplexer_2 (
    .in0(and_1_out), .in1(or_1_out), .in2(xor_1_out), .in3(nor_1_out), .out(multiplexer_2_out), .sel(func2));  // open: en
  Multiplexer #(.select(5), .width(16)) multiplexer_3 (
    .in0(multiplexer_2_out), .in1(multiplexer_1_out), .in4(and_2_out), .in5(or_2_out), .in6(xor_2_out),
    .in7(adder_2_out), .in8(shifter_1_out), .in9(shifter_2_out), .in10(shifter_3_out), .in11(shifter_4_out),
    .in12(adder_2_out), .in13(adder_2_out), .in14(bit_extender_7_out), .in15(bit_extender_8_out),
    .in16(shifter_5_out), .out(Output), .sel(Opcode));  // open: in2, in3, in17, in18, in19, in20, in21, in22, in23, in24, in25, in26, in27, in28, in29, in30, in31, en

  // Notes on the sheet:
  //   ANDI
  //   ORI
  //   XORI
  //   ADDI
  //   and 000
  //   or 001
  //   xor 010
  //   nor 011
  //   add 100
  //   sub 101
  //   SLT
  //   SLTU
  //   SLL
  //   SRL
  //   SRA
  //   ROR
  //   LUI
endmodule

module test (
  input  lwCounter,
  input  lw,
  output stall
);

  wire not_1_out;

  not not_1 (not_1_out, lwCounter);
  and and_1 (stall, not_1_out, lw);
endmodule

// Delay
module Delay_79_Buffer (
  input  in,
  output out
);

  wire buffer_1_out, buffer_2_out, buffer_3_out, buffer_4_out, buffer_5_out, buffer_6_out, buffer_7_out,
       buffer_8_out, buffer_9_out, buffer_10_out, buffer_11_out, buffer_12_out, buffer_13_out, buffer_14_out,
       buffer_15_out, buffer_16_out, buffer_17_out, buffer_18_out, buffer_19_out, buffer_20_out,
       buffer_21_out, buffer_22_out, buffer_23_out, buffer_24_out, buffer_25_out, buffer_26_out,
       buffer_27_out, buffer_28_out, buffer_29_out, buffer_30_out, buffer_31_out, buffer_32_out,
       buffer_33_out, buffer_34_out, buffer_35_out, buffer_36_out, buffer_37_out, buffer_38_out,
       buffer_39_out, buffer_40_out, buffer_41_out, buffer_42_out, buffer_43_out, buffer_44_out,
       buffer_45_out, buffer_46_out, buffer_47_out, buffer_48_out, buffer_49_out, buffer_50_out,
       buffer_51_out, buffer_52_out, buffer_53_out, buffer_54_out, buffer_55_out, buffer_56_out,
       buffer_57_out, buffer_58_out, buffer_59_out, buffer_60_out, buffer_61_out, buffer_63_out,
       buffer_64_out, buffer_65_out, buffer_66_out, buffer_67_out, buffer_68_out, buffer_69_out,
       buffer_70_out, buffer_71_out, buffer_72_out, buffer_73_out, buffer_74_out, buffer_75_out,
       buffer_76_out, buffer_77_out, buffer_78_out, buffer_79_out;

  buf buffer_1 (buffer_1_out, buffer_3_out);
  buf buffer_2 (buffer_2_out, buffer_4_out);
  buf buffer_3 (buffer_3_out, buffer_2_out);
  buf buffer_4 (buffer_4_out, buffer_65_out);
  buf buffer_5 (buffer_5_out, buffer_6_out);
  buf buffer_6 (buffer_6_out, buffer_8_out);
  buf buffer_7 (buffer_7_out, buffer_9_out);
  buf buffer_8 (buffer_8_out, buffer_7_out);
  buf buffer_9 (buffer_9_out, buffer_69_out);
  buf buffer_10 (buffer_10_out, buffer_13_out);
  buf buffer_11 (buffer_11_out, buffer_72_out);
  buf buffer_12 (buffer_12_out, buffer_11_out);
  buf buffer_13 (buffer_13_out, buffer_12_out);
  buf buffer_14 (buffer_14_out, buffer_15_out);
  buf buffer_15 (buffer_15_out, buffer_16_out);
  buf buffer_16 (buffer_16_out, buffer_78_out);
  buf buffer_17 (buffer_17_out, buffer_14_out);
  buf buffer_18 (buffer_18_out, in);
  buf buffer_19 (buffer_19_out, buffer_20_out);
  buf buffer_20 (buffer_20_out, buffer_18_out);
  buf buffer_21 (buffer_21_out, buffer_19_out);
  buf buffer_22 (buffer_22_out, buffer_1_out);
  buf buffer_23 (buffer_23_out, buffer_22_out);
  buf buffer_24 (buffer_24_out, buffer_23_out);
  buf buffer_25 (buffer_25_out, buffer_24_out);
  buf buffer_26 (buffer_26_out, buffer_29_out);
  buf buffer_27 (buffer_27_out, buffer_28_out);
  buf buffer_28 (buffer_28_out, buffer_26_out);
  buf buffer_29 (buffer_29_out, buffer_5_out);
  buf buffer_30 (buffer_30_out, buffer_32_out);
  buf buffer_31 (buffer_31_out, buffer_10_out);
  buf buffer_32 (buffer_32_out, buffer_33_out);
  buf buffer_33 (buffer_33_out, buffer_31_out);
  buf buffer_34 (buffer_34_out, buffer_36_out);
  buf buffer_35 (buffer_35_out, buffer_17_out);
  buf buffer_36 (buffer_36_out, buffer_37_out);
  buf buffer_37 (buffer_37_out, buffer_35_out);
  buf buffer_38 (buffer_38_out, buffer_41_out);
  buf buffer_39 (buffer_39_out, buffer_38_out);
  buf buffer_40 (buffer_40_out, buffer_21_out);
  buf buffer_41 (buffer_41_out, buffer_40_out);
  buf buffer_42 (buffer_42_out, buffer_44_out);
  buf buffer_43 (buffer_43_out, buffer_45_out);
  buf buffer_44 (buffer_44_out, buffer_43_out);
  buf buffer_45 (buffer_45_out, buffer_25_out);
  buf buffer_46 (buffer_46_out, buffer_48_out);
  buf buffer_47 (buffer_47_out, buffer_46_out);
  buf buffer_48 (buffer_48_out, buffer_49_out);
  buf buffer_49 (buffer_49_out, buffer_27_out);
  buf buffer_50 (buffer_50_out, buffer_51_out);
  buf buffer_51 (buffer_51_out, buffer_52_out);
  buf buffer_52 (buffer_52_out, buffer_30_out);
  buf buffer_53 (buffer_53_out, buffer_50_out);
  buf buffer_54 (buffer_54_out, buffer_57_out);
  buf buffer_55 (buffer_55_out, buffer_34_out);
  buf buffer_56 (buffer_56_out, buffer_55_out);
  buf buffer_57 (buffer_57_out, buffer_56_out);
  buf buffer_58 (buffer_58_out, buffer_60_out);
  buf buffer_59 (buffer_59_out, buffer_39_out);
  buf buffer_60 (buffer_60_out, buffer_61_out);
  buf buffer_61 (buffer_61_out, buffer_59_out);
  buf buffer_62 (out, buffer_63_out);
  buf buffer_63 (buffer_63_out, buffer_42_out);
  buf buffer_64 (buffer_64_out, buffer_66_out);
  buf buffer_65 (buffer_65_out, buffer_67_out);
  buf buffer_66 (buffer_66_out, buffer_47_out);
  buf buffer_67 (buffer_67_out, buffer_64_out);
  buf buffer_68 (buffer_68_out, buffer_53_out);
  buf buffer_69 (buffer_69_out, buffer_70_out);
  buf buffer_70 (buffer_70_out, buffer_71_out);
  buf buffer_71 (buffer_71_out, buffer_68_out);
  buf buffer_72 (buffer_72_out, buffer_74_out);
  buf buffer_73 (buffer_73_out, buffer_54_out);
  buf buffer_74 (buffer_74_out, buffer_75_out);
  buf buffer_75 (buffer_75_out, buffer_73_out);
  buf buffer_76 (buffer_76_out, buffer_77_out);
  buf buffer_77 (buffer_77_out, buffer_79_out);
  buf buffer_78 (buffer_78_out, buffer_76_out);
  buf buffer_79 (buffer_79_out, buffer_58_out);
endmodule

// 1st
module _1st_stage (
  input  [15:0] instr_input,
  input  clock,
  input  stall,
  input  clear,
  output [15:0] instr_input_2
);

  wire not_1_out;

  not not_1 (not_1_out, stall);
  Register #(.width(16)) register_1 (.D(instr_input), .en(not_1_out), .Q(instr_input_2), .clk(clock), .clr(clear));
endmodule

// 2nd
module _2nd_stage (
  input  clock,
  input  stall,
  input  [2:0] rd3,
  input  [2:0] rt3,
  input  [2:0] rs3,
  input  [11:0] pc_1_branch,
  input  [1:0] func2,
  input  [4:0] immediate5,
  input  [10:0] immediate11,
  input  [4:0] opcode,
  input  r7_write,
  input  write,
  input  single_reg_instr,
  input  single_third_reg_instr,
  input  r1_write,
  input  alu_source,
  input  store_memory,
  input  clear,
  output [2:0] rd3_2,
  output [2:0] rt3_2,
  output [2:0] rs3_2,
  output [11:0] pc_1_branch_2,
  output [1:0] func2_2,
  output [4:0] immediate5_2,
  output [10:0] immediate11_2,
  output [4:0] opcode_2,
  output r7_write_2,
  output write_2,
  output single_reg_instr_2,
  output single_third_reg_instr_2,
  output r1_write_2,
  output alu_source_2,
  output store_memory_2
);

  wire not_1_out;

  not not_1 (not_1_out, stall);
  Register #(.width(3)) register_1 (.D(rd3), .en(not_1_out), .Q(rd3_2), .clk(clock), .clr(clear));
  Register #(.width(3)) register_2 (.D(rt3), .en(not_1_out), .Q(rt3_2), .clk(clock), .clr(clear));
  Register #(.width(3)) register_3 (.D(rs3), .en(not_1_out), .Q(rs3_2), .clk(clock), .clr(clear));
  Register #(.width(12)) register_4 (.D(pc_1_branch), .en(not_1_out), .Q(pc_1_branch_2), .clk(clock), .clr(clear));
  Register #(.width(2)) register_5 (.D(func2), .en(not_1_out), .Q(func2_2), .clk(clock), .clr(clear));
  Register #(.width(5)) register_6 (.D(immediate5), .en(not_1_out), .Q(immediate5_2), .clk(clock), .clr(clear));
  Register #(.width(11)) register_7 (.D(immediate11), .en(not_1_out), .Q(immediate11_2), .clk(clock), .clr(clear));
  Register #(.width(5)) register_8 (.D(opcode), .en(not_1_out), .Q(opcode_2), .clk(clock), .clr(clear));
  Register #(.width(1)) register_9 (.D(r7_write), .en(not_1_out), .Q(r7_write_2), .clk(clock), .clr(clear));
  Register #(.width(1)) register_10 (.D(write), .en(not_1_out), .Q(write_2), .clk(clock), .clr(clear));
  Register #(.width(1)) register_11 (
    .D(single_reg_instr), .en(not_1_out), .Q(single_reg_instr_2), .clk(clock), .clr(clear));
  Register #(.width(1)) register_12 (
    .D(single_third_reg_instr), .en(not_1_out), .Q(single_third_reg_instr_2), .clk(clock), .clr(clear));
  Register #(.width(1)) register_13 (.D(r1_write), .en(not_1_out), .Q(r1_write_2), .clk(clock), .clr(clear));
  Register #(.width(1)) register_14 (.D(alu_source), .en(not_1_out), .Q(alu_source_2), .clk(clock), .clr(clear));
  Register #(.width(1)) register_15 (.D(store_memory), .en(not_1_out), .Q(store_memory_2), .clk(clock), .clr(clear));
endmodule

// 3rd
module _3rd_stage (
  input  clock,
  input  stall,
  input  [11:0] pc_1_branch,
  input  [15:0] output_0,
  input  [15:0] output_1,
  input  [1:0] func2,
  input  [4:0] imm5,
  input  [10:0] imm11,
  input  [4:0] opcode,
  input  store_memory,
  input  alu_source,
  input  [2:0] write_register,
  input  r7_write,
  input  write,
  input  single_reg_instr,
  input  single_third_reg_instr,
  input  r1_write,
  input  clear,
  output [11:0] pc_1_branch_2,
  output [15:0] output_0_2,
  output [15:0] output_1_2,
  output [1:0] func2_2,
  output [4:0] imm5_2,
  output [10:0] imm11_2,
  output [4:0] opcode_2,
  output store_memory_2,
  output alu_source_2,
  output [2:0] write_register_2,
  output r7_write_2,
  output write_2,
  output single_reg_instr_2,
  output single_third_reg_instr_2,
  output r1_write_2
);

  wire not_1_out;

  not not_1 (not_1_out, stall);
  Register #(.width(12)) register_1 (.D(pc_1_branch), .en(not_1_out), .Q(pc_1_branch_2), .clk(clock), .clr(clear));
  Register #(.width(16)) register_2 (.D(output_0), .en(not_1_out), .Q(output_0_2), .clk(clock), .clr(clear));
  Register #(.width(16)) register_3 (.D(output_1), .en(not_1_out), .Q(output_1_2), .clk(clock), .clr(clear));
  Register #(.width(2)) register_4 (.D(func2), .en(not_1_out), .Q(func2_2), .clk(clock), .clr(clear));
  Register #(.width(5)) register_5 (.D(imm5), .en(not_1_out), .Q(imm5_2), .clk(clock), .clr(clear));
  Register #(.width(11)) register_6 (.D(imm11), .en(not_1_out), .Q(imm11_2), .clk(clock), .clr(clear));
  Register #(.width(5)) register_7 (.D(opcode), .en(not_1_out), .Q(opcode_2), .clk(clock), .clr(clear));
  Register #(.width(1)) register_8 (.D(store_memory), .en(not_1_out), .Q(store_memory_2), .clk(clock), .clr(clear));
  Register #(.width(1)) register_9 (.D(alu_source), .en(not_1_out), .Q(alu_source_2), .clk(clock), .clr(clear));
  Register #(.width(3)) register_10 (
    .D(write_register), .en(not_1_out), .Q(write_register_2), .clk(clock), .clr(clear));
  Register #(.width(1)) register_11 (.D(r7_write), .en(not_1_out), .Q(r7_write_2), .clk(clock), .clr(clear));
  Register #(.width(1)) register_12 (.D(write), .en(not_1_out), .Q(write_2), .clk(clock), .clr(clear));
  Register #(.width(1)) register_13 (
    .D(single_reg_instr), .en(not_1_out), .Q(single_reg_instr_2), .clk(clock), .clr(clear));
  Register #(.width(1)) register_14 (
    .D(single_third_reg_instr), .en(not_1_out), .Q(single_third_reg_instr_2), .clk(clock), .clr(clear));
  Register #(.width(1)) register_15 (.D(r1_write), .en(not_1_out), .Q(r1_write_2), .clk(clock), .clr(clear));
endmodule

// 4th
module _4th_stage (
  input  clock,
  input  stall,
  input  [11:0] pc_1_branch,
  input  alu_source,
  input  [15:0] alu_output,
  input  [15:0] memory_output,
  input  [2:0] write_register,
  input  r7_write,
  input  write,
  input  single_reg_instr,
  input  single_third_reg_instr,
  input  r1_write,
  input  [4:0] imm5,
  input  bb,
  input  clear,
  output [11:0] pc_1_branch_2,
  output alu_source_2,
  output [15:0] alu_output_2,
  output [15:0] memory_output_2,
  output [2:0] write_register_2,
  output r7_write_2,
  output write_2,
  output single_reg_instr_2,
  output single_third_reg_instr_2,
  output r1_write_2,
  output [4:0] imm5_2,
  output bb_2
);

  wire not_1_out;

  not not_1 (not_1_out, stall);
  Register #(.width(12)) register_1 (.D(pc_1_branch), .en(not_1_out), .Q(pc_1_branch_2), .clk(clock), .clr(clear));
  Register #(.width(1)) register_2 (.D(alu_source), .en(not_1_out), .Q(alu_source_2), .clk(clock), .clr(clear));
  Register #(.width(16)) register_3 (.D(alu_output), .en(not_1_out), .Q(alu_output_2), .clk(clock), .clr(clear));
  Register #(.width(16)) register_4 (.D(memory_output), .en(not_1_out), .Q(memory_output_2), .clk(clock), .clr(clear));
  Register #(.width(3)) register_5 (.D(write_register), .en(not_1_out), .Q(write_register_2), .clk(clock), .clr(clear));
  Register #(.width(1)) register_6 (.D(r7_write), .en(not_1_out), .Q(r7_write_2), .clk(clock), .clr(clear));
  Register #(.width(1)) register_7 (.D(write), .en(not_1_out), .Q(write_2), .clk(clock), .clr(clear));
  Register #(.width(1)) register_8 (
    .D(single_reg_instr), .en(not_1_out), .Q(single_reg_instr_2), .clk(clock), .clr(clear));
  Register #(.width(1)) register_9 (
    .D(single_third_reg_instr), .en(not_1_out), .Q(single_third_reg_instr_2), .clk(clock), .clr(clear));
  Register #(.width(1)) register_10 (.D(r1_write), .en(not_1_out), .Q(r1_write_2), .clk(clock), .clr(clear));
  Register #(.width(5)) register_11 (.D(imm5), .en(not_1_out), .Q(imm5_2), .clk(clock), .clr(clear));
  Register #(.width(1)) register_12 (.D(bb), .en(not_1_out), .Q(bb_2), .clk(clock), .clr(clear));
endmodule

// A/M
module alu_mem_MUX (
  input  [15:0] memory_output,
  input  [15:0] alu_output,
  input  alu_source,
  output [15:0] register_input
);

  Multiplexer #(.width(16), .enable("false")) multiplexer_1 (
    .in0(memory_output), .in1(alu_output), .out(register_input), .sel(alu_source));
endmodule

// hazard
module hazard_unit (
  input  [4:0] opcode_3,
  input  beq_bne_flag,
  output stall,
  output clear
);

  wire JR_out, not_1_out, not_2_out, not_3_out, not_4_out;

  not not_1 (not_1_out, opcode_3[0]);
  not not_2 (not_2_out, opcode_3[2]);
  not not_3 (not_3_out, opcode_3[3]);
  not not_4 (not_4_out, opcode_3[4]);
  and JR (JR_out, not_1_out, opcode_3[1], not_2_out, not_3_out, not_4_out);
  buf or_1 (clear, beq_bne_flag);  // OR_Gate

  assign stall = 1'b0;
endmodule

module hazard_unit_eski (
  input  [4:0] opcode,
  input  clock,
  output stall
);

  wire and_2_out, and_3_out, comparator_1_eq, comparator_1_gt, comparator_2_eq, comparator_2_gt, lw_out,
       not_1_out, not_2_out, not_3_out, not_4_out, not_5_out, not_6_out, not_7_out, or_1_out, or_2_out,
       or_3_out, or_4_out, sw_out;
  wire [2:0] counter_1_q, counter_2_q;

  not not_1 (not_1_out, opcode[0]);
  not not_2 (not_2_out, opcode[1]);
  not not_3 (not_3_out, opcode[4]);
  not not_4 (not_4_out, opcode[1]);
  not not_5 (not_5_out, opcode[4]);
  and lw (lw_out, not_1_out, not_2_out, opcode[2], opcode[3], not_3_out);
  and sw (sw_out, opcode[0], not_4_out, opcode[2], opcode[3], not_5_out);
  // AND_Gate beq is placed but not wired
  // AND_Gate and_1 is placed but not wired
  or or_1 (or_1_out, or_3_out, sw_out);
  Counter #(.width(3), .max('h7)) counter_1 (
    .count(or_2_out), .Q(counter_1_q), .clk(clock), .clr(comparator_2_gt));  // open: load, D, carry
  or or_2 (or_2_out, or_4_out, lw_out);
  Counter #(.width(3), .max('h7)) counter_2 (
    .count(or_1_out), .Q(counter_2_q), .clk(clock), .clr(comparator_1_gt));  // open: load, D, carry
  Comparator #(.width(3), .mode("unsigned")) comparator_1 (
    .a(counter_2_q), .b(3'b011), .gt(comparator_1_gt), .eq(comparator_1_eq));  // open: lt
  Comparator #(.width(3), .mode("unsigned")) comparator_2 (
    .a(counter_1_q), .b(3'b011), .gt(comparator_2_gt), .eq(comparator_2_eq));  // open: lt
  or or_3 (or_3_out, comparator_1_gt, comparator_1_eq);
  or or_4 (or_4_out, comparator_2_gt, comparator_2_eq);
  not not_6 (not_6_out, or_4_out);
  not not_7 (not_7_out, or_3_out);
  and and_2 (and_2_out, not_6_out, lw_out);
  and and_3 (and_3_out, sw_out, not_7_out);
  xor xor_1 (stall, and_2_out, and_3_out);
endmodule
